// Logisim project circuit_3.circ as structural Verilog: 1 circuit, main circuit main
module main (
);

  wire Betrag_2_p2, Betrag_2_p4, Betrag_2_p5, Betrag_2_p7, Betrag_p1, Betrag_p2, Betrag_p3, Betrag_p4,
       Betrag_p5, Betrag_p6, Betrag_p7, minus_e_2n_Subtrahierer_p3, minus_e_2n_Subtrahierer_p5,
       minus_e_2n_Subtrahierer_p7, minus_e_2n_Subtrahierer_p9, minus_e_2n_Subtrahierer_p12, MULT_n_p2,
       MULT_n_p4, MULT_n_p6, MULT_n_p7, MULT_n_p8, xor_1_out, xor_2_out, xor_3_out, xor_4_out;

  xor xor_1 (xor_1_out, Betrag_p1, Betrag_2_p2);
  // Even_Parity Betrag: pin names not known; wires that end beside it: Betrag_p1, Betrag_p2, Betrag_p3, Betrag_p4, Betrag_p5, Betrag_p6, Betrag_p7
  xor xor_2 (xor_2_out, minus_e_2n_Subtrahierer_p7, xor_1_out);
  // Even_Parity MULT_n: pin names not known; wires that end beside it: Betrag_p2, MULT_n_p2, Betrag_p6, MULT_n_p4, Betrag_p7, MULT_n_p6, MULT_n_p7, MULT_n_p8
  // Even_Parity minus_e_2n_Subtrahierer: pin names not known; wires that end beside it: MULT_n_p2, xor_1_out, minus_e_2n_Subtrahierer_p3, minus_e_2n_Subtrahierer_p3, minus_e_2n_Subtrahierer_p5, minus_e_2n_Subtrahierer_p5, minus_e_2n_Subtrahierer_p7, MULT_n_p4, minus_e_2n_Subtrahierer_p9, MULT_n_p6, MULT_n_p8, minus_e_2n_Subtrahierer_p12
  xor xor_3 (xor_3_out, minus_e_2n_Subtrahierer_p9, xor_1_out);
  // Even_Parity Betrag_2: pin names not known; wires that end beside it: Betrag_p6, Betrag_2_p2, Betrag_p7, Betrag_2_p4, Betrag_2_p5, MULT_n_p7, Betrag_2_p7
  xor xor_4 (xor_4_out, minus_e_2n_Subtrahierer_p12, xor_1_out);

  // Notes on the sheet:
  //   a_n
  //   e_2n
  //   a_n-1
  //   e_2n-1
  //   ....
  //   ...................
  //   ...................
  //   e_2n-2
  //   a_0
  //   .............
  //   b_n
  //   b_n-1
  //   ...................
  //   ...................
  //   ....
  //   b_0
  //   e_0
endmodule
