// Logisim project Komperator.circ as structural Verilog: 1 circuit, main circuit main
module main (
);

  wire and_1_out, and_2_out, and_4_out, and_5_out, and_6_out, not_1_out, not_2_out, not_3_out, not_4_out,
       not_5_out, not_6_out, or_2_out, undriven, undriven_2, undriven_3, undriven_4, undriven_5, undriven_6,
       xor_1_out, xor_2_out, xor_4_out;

  not not_1 (not_1_out, undriven);
  xor xor_1 (xor_1_out, undriven, undriven_2);
  not not_2 (not_2_out, undriven_3);
  xor xor_2 (xor_2_out, undriven_3, undriven_4);
  // XOR_Gate xor_3 is placed but not wired
  // OR_Gate or_1 is placed but not wired
  not not_3 (not_3_out, undriven_5);
  xor xor_4 (xor_4_out, undriven_5, undriven_6);
  and and_1 (and_1_out, not_1_out, xor_1_out);
  not not_4 (not_4_out, xor_1_out);
  and and_2 (and_2_out, not_2_out, xor_2_out);
  not not_5 (not_5_out, xor_2_out);
  // AND_Gate and_3 is placed but not wired
  and and_4 (and_4_out, not_3_out, xor_4_out);
  not not_6 (not_6_out, xor_4_out);
  and and_5 (and_5_out, and_1_out, not_5_out);
  and and_6 (and_6_out, not_4_out, not_5_out);
  // NOT_Gate not_7 is placed but not wired
  or or_2 (or_2_out, and_5_out, and_2_out);

  // Notes on the sheet:
  //   a_1
  //   b_1
  //   a_2
  //   b_2
  //   a
  //   b
  //   f
  //   g
  //   f
  //   g
endmodule
