// Logisim project circuit_1.circ as structural Verilog: 1 circuit, main circuit main
module main (
);

  wire and_1_out, and_2_out, and_3_out, and_4_out, and_5_out, and_6_out, and_7_out, and_8_out, and_9_out,
       and_10_out, and_11_out, and_12_out, D_Latch_2_p3, D_Latch_3_p3, D_Latch_4_p3, D_Latch_p1, D_Latch_p4,
       not_1_out, not_2_out, or_1_out, or_2_out, or_3_out, undriven, undriven_2, undriven_3;

  not not_1 (not_1_out, undriven);
  not not_2 (not_2_out, undriven_2);
  and and_1 (and_1_out, not_1_out, not_2_out);
  and and_2 (and_2_out, not_2_out, undriven);
  and and_3 (and_3_out, not_1_out, undriven_2);
  and and_4 (and_4_out, undriven_2, undriven);
  and and_5 (and_5_out, undriven_3, and_1_out);
  and and_6 (and_6_out, undriven_3, and_2_out);
  and and_7 (and_7_out, undriven_3, and_3_out);
  and and_8 (and_8_out, undriven_3, and_4_out);
  // Even_Parity D_Latch: pin names not known; wires that end beside it: D_Latch_p1, D_Latch_p1, and_5_out, D_Latch_p4
  // Even_Parity D_Latch_2: pin names not known; wires that end beside it: D_Latch_p1, and_6_out, D_Latch_2_p3
  // Even_Parity D_Latch_3: pin names not known; wires that end beside it: D_Latch_p1, and_7_out, D_Latch_3_p3
  // Even_Parity D_Latch_4: pin names not known; wires that end beside it: D_Latch_p1, and_8_out, D_Latch_4_p3
  and and_9 (and_9_out, D_Latch_p4, and_1_out);
  or or_1 (or_1_out, and_9_out, and_10_out);
  and and_10 (and_10_out, D_Latch_2_p3, and_2_out);
  and and_11 (and_11_out, D_Latch_3_p3, and_3_out);
  or or_2 (or_2_out, and_11_out, and_12_out);
  and and_12 (and_12_out, D_Latch_4_p3, and_4_out);
  or or_3 (or_3_out, or_1_out, or_2_out);

  // Notes on the sheet:
  //   a_0
  //   a_1
  //   d_0
  //   d_1
  //   d_2
  //   d_3
  //   W
  //   D_in
  //   D
  //   W
  //   D
  //   W
  //   D
  //   W
  //   D
  //   W
  //   Q
  //   Q
  //   Q
  //   Q
  //   D_out
endmodule
