// Logisim project muxer.circ as structural Verilog: 1 circuit, main circuit main
module main (
);

  wire multiplexer_1_out, multiplexer_2_out, multiplexer_3_out, multiplexer_4_out, multiplexer_5_out,
       multiplexer_6_out, multiplexer_7_out, undriven, undriven_2, undriven_3, undriven_4, undriven_5;

  Multiplexer #(.enable("false")) multiplexer_1 (
    .in0(multiplexer_2_out), .in1(multiplexer_3_out), .out(multiplexer_1_out), .sel(undriven_3));
  Multiplexer #(.enable("false")) multiplexer_2 (
    .in0(undriven_5), .in1(undriven), .out(multiplexer_2_out), .sel(undriven_4));
  Multiplexer #(.enable("false")) multiplexer_3 (
    .in0(undriven), .in1(undriven_5), .out(multiplexer_3_out), .sel(undriven_4));
  Multiplexer #(.enable("false")) multiplexer_4 (
    .in0(multiplexer_1_out), .in1(multiplexer_5_out), .out(multiplexer_4_out), .sel(undriven_2));
  Multiplexer #(.enable("false")) multiplexer_5 (
    .in0(multiplexer_6_out), .in1(multiplexer_7_out), .out(multiplexer_5_out), .sel(undriven_4));
  Multiplexer #(.enable("false")) multiplexer_6 (
    .in0(undriven), .in1(undriven_5), .out(multiplexer_6_out), .sel(undriven_3));
  Multiplexer #(.enable("false")) multiplexer_7 (
    .in0(undriven_5), .in1(undriven_5), .out(multiplexer_7_out), .sel(undriven_3));

  // Notes on the sheet:
  //   X1
  //   X2
  //   X3
  //   0
  //   1
endmodule
